# Fritzing sketch esp32_arduino_circuit (saved by Fritzing 0.9.5d)

parts:
  Part1 = Arduino Uno (Rev3) - ICSP
  Part2 = Logic Level Converter
  U1 = ESP32S-HiLetgo [part_number=ESP32S-HiLetgo]

nets:
  N1: Part1.5V, Part2.HV
  GND: Part1.GND, Part2.GND, U1.GND
  N2: Part1.D0/RX, Part2.RX2_HV
  N3: Part1.D1/TX, Part2.TX2_HV
  N4: Part2.TX2_LV, U1.GPIO16
  N5: Part2.RX2_LV, U1.GPIO17
  N6: Part2.LV, U1.3.3

custom parts:
  ESP32S-HiLetgo: HiLetgo ESP-WROOM-32 ESP32 ESP-32S Development Board 2.4GHz Dual-Mode WiFi + Bluetooth Dual Cores Microcontroller The ESP32 integrated with Antenna switches, RF Balun, power amplifiers, low-noise amplifiers, filters, and management modules, and the entire solution occupies the least area of PCB. 2.4 GHz Wi-Fi plus Bluetooth dual-mode chip, with TSMC Ultra-low power consumption 40nm technology,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
